// Logisim project rv32I_datapath.circ as structural Verilog: 18 circuits, main circuit Data path
// ALU
module ALUonlyIR (
  input  [31:0] RS2,
  input  [31:0] RS1,
  input  add_sub_sel,
  input  Shift_select,
  input  [2:0] Function_3,
  output Overflow,
  output [31:0] ALU_OUT
);

  wire comparator_1_lt, comparator_2_lt, multiplexer_3_out;
  wire [31:0] adder_sub_1_output, and_1_out, bit_extender_1_out, multiplexer_1_out, multiplexer_2_out,
       multiplexer_5_out, multiplexer_6_out, multiplexer_7_out, or_1_out, shifter_1_out, shifters_1_out,
       xor_1_out;

  ADder_sub adder_sub_1 (.Select(add_sub_sel), .A(RS2), .B(RS1), .Cout(Overflow), .Output(adder_sub_1_output));
  Shifter #(.width(32)) shifter_1 (.in(RS2), .\dist (RS1[4:0]), .out(shifter_1_out));
  Multiplexer #(.width(32), .enable("false")) multiplexer_1 (
    .in0(adder_sub_1_output), .in1(shifter_1_out), .out(multiplexer_1_out), .sel(Function_3[0]));
  Multiplexer #(.width(32), .enable("false")) multiplexer_2 (
    .in0(multiplexer_1_out), .in1(bit_extender_1_out), .out(multiplexer_2_out), .sel(Function_3[1]));
  Comparator #(.width(32)) comparator_1 (.a(RS1), .b(RS2), .lt(comparator_1_lt));  // open: gt, eq
  Comparator #(.width(32), .mode("unsigned")) comparator_2 (.a(RS1), .b(RS2), .lt(comparator_2_lt));  // open: gt, eq
  Multiplexer #(.enable("false")) multiplexer_3 (
    .in0(comparator_1_lt), .in1(comparator_2_lt), .out(multiplexer_3_out), .sel(Function_3[0]));
  assign bit_extender_1_out = {{31{1'b0}}, multiplexer_3_out};  // Bit_Extender bit_extender_1
  Multiplexer #(.width(32), .enable("false")) multiplexer_4 (
    .in0(multiplexer_2_out), .in1(multiplexer_6_out), .out(ALU_OUT), .sel(Function_3[2]));
  assign xor_1_out = RS2 ^ RS1;  // XOR_Gate xor_1, 32 bits wide
  Multiplexer #(.width(32), .enable("false")) multiplexer_5 (
    .in0(xor_1_out), .in1(shifters_1_out), .out(multiplexer_5_out), .sel(Function_3[0]));
  shifters shifters_1 (.B(RS1), .A(RS2), .Select(Shift_select), .Out(shifters_1_out));
  Multiplexer #(.width(32), .enable("false")) multiplexer_6 (
    .in0(multiplexer_5_out), .in1(multiplexer_7_out), .out(multiplexer_6_out), .sel(Function_3[1]));
  assign or_1_out = RS2 | RS1;  // OR_Gate or_1, 32 bits wide
  assign and_1_out = RS2 & RS1;  // AND_Gate and_1, 32 bits wide
  Multiplexer #(.width(32), .enable("false")) multiplexer_7 (
    .in0(or_1_out), .in1(and_1_out), .out(multiplexer_7_out), .sel(Function_3[0]));

  // Notes on the sheet:
  //   I AND R TYPE ALU 
endmodule

module ADder_sub (
  input  [31:0] A,
  input  [31:0] B,
  input  Select,
  output Cout,
  output [31:0] Output
);

  wire adder_1_cout, subtractor_1_bout;
  wire [31:0] adder_1_out, subtractor_1_out;

  Multiplexer #(.enable("false")) multiplexer_1 (.in0(adder_1_cout), .in1(subtractor_1_bout), .out(Cout), .sel(Select));
  Adder #(.width(32)) adder_1 (.a(A), .b(B), .out(adder_1_out), .cout(adder_1_cout));  // open: cin
  Subtractor #(.width(32)) subtractor_1 (.a(A), .b(B), .out(subtractor_1_out), .bout(subtractor_1_bout));  // open: bin
  Multiplexer #(.width(32), .enable("false")) multiplexer_2 (
    .in0(adder_1_out), .in1(subtractor_1_out), .out(Output), .sel(Select));
endmodule

// Reg file
module I_or_R_select (
  input  write_enable,
  input  [4:0] in_2,
  input  [4:0] in_3,
  input  [4:0] in_4,
  input  [11:0] Immidiate,
  input  Select_I_R,
  input  ADD_sub,
  input  Shifter,
  input  [2:0] Function_3,
  output Cout,
  output [31:0] DataOut
);

  wire clock_out;
  wire [31:0] aluonlyir_1_p8, bit_extender_1_out, multiplexer_1_out, register_file_1_busb;

  Clock clock (.out(clock_out));
  assign bit_extender_1_out = {{20{Immidiate[11]}}, Immidiate};  // Bit_Extender bit_extender_1
  Multiplexer #(.width(32), .enable("false")) multiplexer_1 (
    .in0(bit_extender_1_out), .in1(register_file_1_busb), .out(multiplexer_1_out), .sel(Select_I_R));
  // ALUonlyIR aluonlyir_1: pin names not known; wires that end beside it: ADD_sub, Shifter, Function_3[0], Function_3[1], Function_3[2], multiplexer_1_out, DataOut, aluonlyir_1_p8, Cout
  Register_file register_file_1 (
    .clock(clock_out), .Wenable(write_enable), .DataIn(DataOut), .BusA(aluonlyir_1_p8),
    .BusB(register_file_1_busb), .RD(in_2), .RS2(in_4), .RS1(in_3));

  // Other names for the same wires on the sheet: RA[4:0] = in_3; RB[4:0] = in_4; RW[4:0] = in_2
endmodule

module Register_file (
  input  clock,
  input  [31:0] DataIn,
  input  Wenable,
  input  [4:0] RD,
  input  [4:0] RS2,
  input  [4:0] RS1,
  output [31:0] BusB,
  output [31:0] BusA
);

  wire EN1, EN2, EN3, EN4, EN5, EN6, EN7, EN8, EN9, EN10, EN11, EN12, EN13, EN14, EN15, EN16, EN17, EN18,
       EN19, EN20, EN21, EN22, EN23, EN24, EN25, EN26, EN27, EN28, EN29, EN30, EN31;
  wire [31:0] Out0, Out1, Out2, Out3, Out4, Out5, Out6, Out7, Out8, Out9, Out10, Out11, Out12, Out13, Out14,
       Out15, Out16, Out17, Out18, Out19, Out20, Out21, Out22, Out23, Out24, Out25, Out26, Out27, Out28,
       Out29, Out30, Out31;

  Register #(.width(32)) _0 (.D({32{1'b0}}), .en(EN1), .Q(Out0), .clk(clock));  // open: clr
  Register #(.width(32)) _11 (.D(DataIn), .en(EN11), .Q(Out11), .clk(clock));  // open: clr
  Register #(.width(32)) _22 (.D(DataIn), .en(EN22), .Q(Out22), .clk(clock));  // open: clr
  Demultiplexer #(.select(5), .enable("false")) demultiplexer_1 (
    .out1(EN1), .out2(EN2), .out3(EN3), .out4(EN4), .out5(EN5), .out6(EN6), .out7(EN7), .out8(EN8),
    .out9(EN9), .out10(EN10), .out11(EN11), .out12(EN12), .out13(EN13), .out14(EN14), .out15(EN15),
    .out16(EN16), .out17(EN17), .out18(EN18), .out19(EN19), .out20(EN20), .out21(EN21), .out22(EN22),
    .out23(EN23), .out24(EN24), .out25(EN25), .out26(EN26), .out27(EN27), .out28(EN28), .out29(EN29),
    .out30(EN30), .out31(EN31), .in(Wenable), .sel(RD));  // open: out0
  Register #(.width(32)) _1 (.D(DataIn), .en(EN1), .Q(Out1), .clk(clock));  // open: clr
  Register #(.width(32)) _12 (.D(DataIn), .en(EN12), .Q(Out12), .clk(clock));  // open: clr
  Register #(.width(32)) _23 (.D(DataIn), .en(EN23), .Q(Out23), .clk(clock));  // open: clr
  Register #(.width(32)) _2 (.D(DataIn), .en(EN2), .Q(Out2), .clk(clock));  // open: clr
  Register #(.width(32)) _24 (.D(DataIn), .en(EN24), .Q(Out24), .clk(clock));  // open: clr
  Register #(.width(32)) _3 (.D(DataIn), .en(EN3), .Q(Out3), .clk(clock));  // open: clr
  Register #(.width(32)) _13 (.D(DataIn), .en(EN13), .Q(Out13), .clk(clock));  // open: clr
  Register #(.width(32)) _14 (.D(DataIn), .en(EN14), .Q(Out14), .clk(clock));  // open: clr
  Register #(.width(32)) _25 (.D(DataIn), .en(EN25), .Q(Out25), .clk(clock));  // open: clr
  Multiplexer #(.select(5), .width(32), .enable("false")) multiplexer_1 (
    .in0(Out0), .in1(Out1), .in2(Out2), .in3(Out3), .in4(Out4), .in5(Out5), .in6(Out6), .in7(Out7),
    .in8(Out8), .in9(Out9), .in10(Out10), .in11(Out11), .in12(Out12), .in13(Out13), .in14(Out14),
    .in15(Out15), .in16(Out16), .in17(Out17), .in18(Out18), .in19(Out19), .in20(Out20), .in21(Out21),
    .in22(Out22), .in23(Out23), .in24(Out24), .in25(Out25), .in26(Out26), .in27(Out27), .in28(Out28),
    .in29(Out29), .in30(Out30), .in31(Out31), .out(BusB), .sel(RS2));
  Register #(.width(32)) _4 (.D(DataIn), .en(EN4), .Q(Out4), .clk(clock));  // open: clr
  Register #(.width(32)) _26 (.D(DataIn), .en(EN26), .Q(Out26), .clk(clock));  // open: clr
  Register #(.width(32)) _5 (.D(DataIn), .en(EN5), .Q(Out5), .clk(clock));  // open: clr
  Register #(.width(32)) _15 (.D(DataIn), .en(EN15), .Q(Out15), .clk(clock));  // open: clr
  Register #(.width(32)) _27 (.D(DataIn), .en(EN27), .Q(Out27), .clk(clock));  // open: clr
  Register #(.width(32)) _6 (.D(DataIn), .en(EN6), .Q(Out6), .clk(clock));  // open: clr
  Multiplexer #(.select(5), .width(32), .enable("false")) multiplexer_2 (
    .in0(Out0), .in1(Out1), .in2(Out2), .in3(Out3), .in4(Out4), .in5(Out5), .in6(Out6), .in7(Out7),
    .in8(Out8), .in9(Out9), .in10(Out10), .in11(Out11), .in12(Out12), .in13(Out13), .in14(Out14),
    .in15(Out15), .in16(Out16), .in17(Out17), .in18(Out18), .in19(Out19), .in20(Out20), .in21(Out21),
    .in22(Out22), .in23(Out23), .in24(Out24), .in25(Out25), .in26(Out26), .in27(Out27), .in28(Out28),
    .in29(Out29), .in30(Out30), .in31(Out31), .out(BusA), .sel(RS1));
  Register #(.width(32)) _16 (.D(DataIn), .en(EN16), .Q(Out16), .clk(clock));  // open: clr
  Register #(.width(32)) _28 (.D(DataIn), .en(EN28), .Q(Out28), .clk(clock));  // open: clr
  Register #(.width(32)) _7 (.D(DataIn), .en(EN7), .Q(Out7), .clk(clock));  // open: clr
  Register #(.width(32)) _17 (.D(DataIn), .en(EN17), .Q(Out17), .clk(clock));  // open: clr
  Register #(.width(32)) _29 (.D(DataIn), .en(EN29), .Q(Out29), .clk(clock));  // open: clr
  Register #(.width(32)) _8 (.D(DataIn), .en(EN8), .Q(Out8), .clk(clock));  // open: clr
  Register #(.width(32)) _18 (.D(DataIn), .en(EN18), .Q(Out18), .clk(clock));  // open: clr
  Register #(.width(32)) _30 (.D(DataIn), .en(EN30), .Q(Out30), .clk(clock));  // open: clr
  Register #(.width(32)) _9 (.D(DataIn), .en(EN9), .Q(Out9), .clk(clock));  // open: clr
  Register #(.width(32)) _19 (.D(DataIn), .en(EN19), .Q(Out19), .clk(clock));  // open: clr
  Register #(.width(32)) _31 (.D(DataIn), .en(EN31), .Q(Out31), .clk(clock));  // open: clr
  Register #(.width(32)) _20 (.D(DataIn), .en(EN20), .Q(Out20), .clk(clock));  // open: clr
  Register #(.width(32)) _10 (.D(DataIn), .en(EN10), .Q(Out10), .clk(clock));  // open: clr
  Register #(.width(32)) _21 (.D(DataIn), .en(EN21), .Q(Out21), .clk(clock));  // open: clr

  // Other names for the same wires on the sheet: Clk = clock; In1[31:0] = DataIn; IN2[31:0] = DataIn;
  //   In3[31:0] = DataIn; In4[31:0] = DataIn; In5[31:0] = DataIn; In6[31:0] = DataIn; In7[31:0] = DataIn;
  //   In8[31:0] = DataIn; In9[31:0] = DataIn; In10[31:0] = DataIn; In11[31:0] = DataIn; In12[31:0] = DataIn;
  //   In13[31:0] = DataIn; In14[31:0] = DataIn; In15[31:0] = DataIn; In16[31:0] = DataIn; In17[31:0] = DataIn;
  //   In18[31:0] = DataIn; In19[31:0] = DataIn; In20[31:0] = DataIn; In21[31:0] = DataIn; In22[31:0] = DataIn;
  //   In23[31:0] = DataIn; In24[31:0] = DataIn; In25[31:0] = DataIn; In26[31:0] = DataIn; In27[31:0] = DataIn;
  //   In28[31:0] = DataIn; In29[31:0] = DataIn; In30[31:0] = DataIn; In31[31:0] = DataIn

  // Notes on the sheet:
  //   ONE to many
  //   Many TO ONE
  //   REGISTER FILE 
endmodule

module shifters (
  input  [31:0] B,
  input  [31:0] A,
  input  Select,
  output [31:0] Out
);

  wire [31:0] shifter_1_out, shifter_2_out;

  Shifter #(.width(32), .shift("lr")) shifter_1 (.in(B), .\dist (A[4:0]), .out(shifter_1_out));
  Multiplexer #(.width(32), .enable("false")) multiplexer_1 (
    .in0(shifter_1_out), .in1(shifter_2_out), .out(Out), .sel(Select));
  Shifter #(.width(32), .shift("ar")) shifter_2 (.in(B), .\dist (A[4:0]), .out(shifter_2_out));
endmodule

module CU (
  input  [6:0] Opcode,
  input  Do_branch,
  input  [2:0] Func_3,
  output write_enable,
  output Imem_src,
  output Select_I_R,
  output BrnachINS,
  output PC_src,
  output ADD_sub,
  output Shifter,
  output [2:0] Function_3
);

  wire and_2_out, not_1_out, not_2_out, not_3_out, not_4_out;

  not not_1 (not_1_out, Opcode[4]);
  not not_2 (not_2_out, Opcode[6]);
  and and_1 (Imem_src, not_1_out, Opcode[5], Opcode[6]);
  not not_3 (not_3_out, Opcode[6]);
  and and_2 (and_2_out, not_3_out, Opcode[5], Opcode[4]);
  not not_4 (not_4_out, Opcode[4]);
  and and_3 (BrnachINS, not_4_out, Opcode[5], Opcode[6]);
  and and_4 (write_enable, Opcode[4], not_2_out);
  or or_1 (Select_I_R, Imem_src, and_2_out);

  assign Function_3 = Func_3;
  assign PC_src = Do_branch;
  assign Shifter = ADD_sub;
endmodule

module Decoder (
  input  [31:0] _32_bit_INS,
  input  [1:0] Imm_SRC,
  output [6:0] Opcode,
  output [4:0] Rd,
  output [4:0] Rs1,
  output [4:0] Rs2,
  output [2:0] Func_3,
  output [6:0] Func7,
  output [4:0] RD_Stroe,
  output [19:0] LUI_imm,
  output [19:0] Jal_Imm,
  output [11:0] Immidiate
);

  Multiplexer #(.select(2), .width(12), .enable("false")) multiplexer_1 (
    .in0(_32_bit_INS[31:20]), .in1({_32_bit_INS[31], _32_bit_INS[7], _32_bit_INS[30:25], _32_bit_INS[11:8]}),
    .in2({_32_bit_INS[31:25], _32_bit_INS[11:7]}), .in3(_32_bit_INS[31:20]), .out(Immidiate), .sel(Imm_SRC));

  assign Func7 = _32_bit_INS[31:25];
  assign Func_3 = _32_bit_INS[14:12];
  assign Jal_Imm = {_32_bit_INS[31], _32_bit_INS[19:12], _32_bit_INS[20], _32_bit_INS[30:21]};
  assign LUI_imm = _32_bit_INS[31:12];
  assign Opcode = _32_bit_INS[6:0];
  assign Rd = _32_bit_INS[11:7];
  assign RD_Stroe = _32_bit_INS[24:20];
  assign Rs1 = _32_bit_INS[19:15];
  assign Rs2 = _32_bit_INS[24:20];

  // Other names for the same wires on the sheet: fun3[2:0] = _32_bit_INS[14:12]; RS_Store[4:0] = _32_bit_INS[19:15];
  //   Rd_Store[4:0] = _32_bit_INS[24:20]

  // Notes on the sheet:
  //   R TYPE
  //   I TYPE 
  //   STORE TYPE
  //   B TYPE
  //   DECODER 
  //   U TYPE
  //   00   I TYPE
  //   01    B TYPE
  //   10    Store 
  //   11    LOAD
endmodule

module Data_path (
  output Overflow
);

  wire Add_sub, Alusrc, branch_yes, Clock_out, Do_branch, From_MEM_ALU, IR_LS, LUI_Nor_immi, LUIPC,
       MEM_write, PC_src, Shifter, Wen;
  wire [1:0] ImIsrc;
  wire [2:0] fun3, Func3InALU;
  wire [4:0] RD, RS1, RS2;
  wire [6:0] func7, Opcode;
  wire [11:0] Immidiate, pc_1_memory_address;
  wire [19:0] Jal_imm, LUI_immidiate;
  wire [23:0] alu_1_alu_out;
  wire [31:0] immidiate_generatator_1_immidite_if_1_bit_ins, immidiate_generatator_1_out, Load_ins_output,
       multiplexer_1_out, multiplexer_2_out, multiplexer_3_out, multiplexer_4_out, multiplexer_5_out,
       pc_1_to_rd, ram_1_data, REG_FILE_busa, REG_FILE_busb, rom_1_data, Store_Ins_data_output;
  wire [31:24] alu_1_alu_out_2;

  PC pc_1 (
    .Memory_address(pc_1_memory_address), .Immidiate(multiplexer_1_out), .CLK(Clock_out), .PC_SRC(PC_src),
    .TO_RD(pc_1_to_rd));
  Clock Clock (.out(Clock_out));
  Multiplexer #(.width(32), .enable("false")) multiplexer_1 (
    .in0(immidiate_generatator_1_immidite_if_1_bit_ins), .in1(immidiate_generatator_1_out),
    .out(multiplexer_1_out), .sel(LUIPC));
  immidiate_generatator immidiate_generatator_1 (
    .OUT(immidiate_generatator_1_out), .Immidite_if_1_bit_ins(immidiate_generatator_1_immidite_if_1_bit_ins),
    .IMM___LUI_IMM(LUI_Nor_immi), .Immidiate(Immidiate), .LUI_Immidiate(LUI_immidiate));
  ROM #(.addrWidth(12), .dataWidth(32)) rom_1 (.addr(pc_1_memory_address), .data(rom_1_data));  // open: sel
  // Probe on multiplexer_2_out
  Store_Ins Store_Ins (.Reg_input(REG_FILE_busb), .Fun3(Func3InALU), .Data_Output(Store_Ins_data_output));
  // Probe on RD
  // Probe on RS2
  // Probe on RS1
  // Probe on REG_FILE_busb
  Multiplexer #(.width(32), .enable("false")) multiplexer_2 (
    .in0(immidiate_generatator_1_out), .in1(REG_FILE_busb), .out(multiplexer_2_out), .sel(Alusrc));
  ALU alu_1 (
    .Add_sub_sel(Add_sub), .shift_select(Shifter), .Overflow(Overflow), .Fun3(Func3InALU),
    .DO_Branch(Do_branch), .Rs1(REG_FILE_busa), .Rs2(multiplexer_2_out), .BranchIns_1_0(branch_yes),
    .ALU_OUT({alu_1_alu_out_2, alu_1_alu_out}), .IR___LS(IR_LS));
  // Probe on multiplexer_3_out
  Register_file REG_FILE (
    .clock(Clock_out), .Wenable(Wen), .DataIn(multiplexer_3_out), .BusA(REG_FILE_busa), .BusB(REG_FILE_busb),
    .RD(RD), .RS2(RS2), .RS1(RS1));
  // Probe on REG_FILE_busa
  // Probe on REG_FILE_busa
  // Probe on {alu_1_alu_out_2, alu_1_alu_out}
  RAM #(.addrWidth(24), .dataWidth(32), .bus("separate")) ram_1 (
    .addr(alu_1_alu_out), .din(Store_Ins_data_output), .data(ram_1_data), .str(MEM_write), .clk(Clock_out));  // open: sel, ld, clr
  Multiplexer #(.width(32), .enable("false")) multiplexer_3 (
    .in0(multiplexer_4_out), .in1(pc_1_to_rd), .out(multiplexer_3_out), .sel(LUIPC));
  Multiplexer #(.width(32), .enable("false")) multiplexer_4 (
    .in0(multiplexer_5_out), .in1(immidiate_generatator_1_out), .out(multiplexer_4_out), .sel(LUI_Nor_immi));
  Multiplexer #(.width(32), .enable("false")) multiplexer_5 (
    .in0({alu_1_alu_out_2, alu_1_alu_out}), .in1(Load_ins_output), .out(multiplexer_5_out), .sel(From_MEM_ALU));
  Load_ins Load_ins (.Fun3(Func3InALU), .Output(Load_ins_output));  // open: value_from_mem
  Decoder decoder_1 (
    ._32_bit_INS(rom_1_data), .Opcode(Opcode), .Rd(RD), .Rs1(RS1), .Rs2(RS2), .Func_3(fun3), .Func7(func7),
    .Immidiate(Immidiate), .Imm_SRC(ImIsrc), .LUI_imm(LUI_immidiate), .Jal_Imm(Jal_imm));  // open: RD_Stroe
  // Probe on ram_1_data
  CU_2 cu_2_1 (
    .Opcode(Opcode), .Do_branch(Do_branch), .Func_3(fun3), .Func7IN(func7), .From_MEM(From_MEM_ALU),
    .LOAD_STORE_INS(IR_LS), .Reg_Write(Wen), .Imm__src(ImIsrc), .Mem_write(MEM_write), .Select_I_R(Alusrc),
    .BrnachINS(branch_yes), .PC_src(PC_src), .ADD_sub(Add_sub), .Shifter(Shifter), .Function_3(Func3InALU),
    .lui_nor_imm(LUI_Nor_immi), .LUIPC(LUIPC));

  // Notes on the sheet:
  //   IMEM
  //   contents of rom_1 (hex, n*v repeats v):
  //   a00093 1400113 114663 108093 fe000ce3
  //   DATA PATH
  //   DMEM
endmodule

// Immidiate geneator
module immidiate_generatator (
  input  [19:0] LUI_Immidiate,
  input  [11:0] Immidiate,
  input  IMM___LUI_IMM,
  output [31:0] OUT,
  output [31:0] Immidite_if_1_bit_ins
);

  wire [31:0] bit_extender_1_out, imm_generator_for_lui_1__32_bit_out;

  assign bit_extender_1_out = {{20{Immidiate[11]}}, Immidiate};  // Bit_Extender bit_extender_1
  imm_generator_for_LUI imm_generator_for_lui_1 (
    ._20_bit_in(LUI_Immidiate), ._32_bit_out(imm_generator_for_lui_1__32_bit_out));
  Multiplexer #(.width(32), .enable("false")) multiplexer_1 (
    .in0(bit_extender_1_out), .in1(imm_generator_for_lui_1__32_bit_out), .out(OUT), .sel(IMM___LUI_IMM));
  Shifter #(.width(32), .shift("ar")) shifter_1 (.in(OUT), .\dist (5'b00001), .out(Immidite_if_1_bit_ins));
endmodule

module B_type_ALU (
  input  [31:0] Rs1,
  input  [31:0] Rs2,
  input  [2:0] Function_3,
  output DO_B
);

  wire comparator_1_eq, comparator_2_eq, comparator_3_lt, comparator_4_gt, comparator_5_lt, comparator_6_gt,
       not_1_out;

  Comparator #(.width(32)) comparator_1 (.a(Rs1), .b(Rs2), .eq(comparator_1_eq));  // open: gt, lt
  not not_1 (not_1_out, comparator_2_eq);
  Comparator #(.width(32)) comparator_2 (.a(Rs1), .b(Rs2), .eq(comparator_2_eq));  // open: gt, lt
  Comparator #(.width(32)) comparator_3 (.a(Rs1), .b(Rs2), .lt(comparator_3_lt));  // open: gt, eq
  Comparator #(.width(32)) comparator_4 (.a(Rs1), .b(Rs2), .gt(comparator_4_gt));  // open: eq, lt
  Comparator #(.width(32), .mode("unsigned")) comparator_5 (.a(Rs1), .b(Rs2), .lt(comparator_5_lt));  // open: gt, eq
  Comparator #(.width(32)) comparator_6 (.a(Rs1), .b(Rs2), .gt(comparator_6_gt));  // open: eq, lt
  Multiplexer #(.select(3)) multiplexer_1 (
    .in0(comparator_1_eq), .in1(not_1_out), .in2(1'b0), .in3(1'b0), .in4(comparator_3_lt),
    .in5(comparator_4_gt), .in6(comparator_5_lt), .in7(comparator_6_gt), .out(DO_B), .sel(Function_3));  // open: en

  // Notes on the sheet:
  //   B TYPE ALU
endmodule

module I_R_type_ALU (
  input  [31:0] RS2,
  input  [31:0] RS1,
  input  add_sub_sel,
  input  Shift_select,
  input  [2:0] Function_3,
  output Overflow,
  output [31:0] ALU_OUT
);

  wire comparator_1_lt, comparator_2_lt, multiplexer_3_out;
  wire [31:0] adder_sub_1_output, and_1_out, bit_extender_1_out, multiplexer_1_out, multiplexer_2_out,
       multiplexer_5_out, multiplexer_6_out, multiplexer_7_out, or_1_out, shifter_1_out, shifters_1_out,
       xor_1_out;

  ADder_sub adder_sub_1 (.Select(add_sub_sel), .A(RS2), .B(RS1), .Cout(Overflow), .Output(adder_sub_1_output));
  Multiplexer #(.width(32), .enable("false")) multiplexer_1 (
    .in0(adder_sub_1_output), .in1(shifter_1_out), .out(multiplexer_1_out), .sel(Function_3[0]));
  Shifter #(.width(32)) shifter_1 (.in(RS2), .\dist (RS1[4:0]), .out(shifter_1_out));
  Multiplexer #(.width(32), .enable("false")) multiplexer_2 (
    .in0(multiplexer_1_out), .in1(bit_extender_1_out), .out(multiplexer_2_out), .sel(Function_3[1]));
  Comparator #(.width(32)) comparator_1 (.a(RS1), .b(RS2), .lt(comparator_1_lt));  // open: gt, eq
  Multiplexer #(.enable("false")) multiplexer_3 (
    .in0(comparator_1_lt), .in1(comparator_2_lt), .out(multiplexer_3_out), .sel(Function_3[0]));
  assign bit_extender_1_out = {{31{1'b0}}, multiplexer_3_out};  // Bit_Extender bit_extender_1
  Multiplexer #(.width(32), .enable("false")) multiplexer_4 (
    .in0(multiplexer_2_out), .in1(multiplexer_6_out), .out(ALU_OUT), .sel(Function_3[2]));
  Comparator #(.width(32), .mode("unsigned")) comparator_2 (.a(RS1), .b(RS2), .lt(comparator_2_lt));  // open: gt, eq
  assign xor_1_out = RS2 ^ RS1;  // XOR_Gate xor_1, 32 bits wide
  Multiplexer #(.width(32), .enable("false")) multiplexer_5 (
    .in0(xor_1_out), .in1(shifters_1_out), .out(multiplexer_5_out), .sel(Function_3[0]));
  shifters shifters_1 (.B(RS1), .A(RS2), .Select(Shift_select), .Out(shifters_1_out));
  Multiplexer #(.width(32), .enable("false")) multiplexer_6 (
    .in0(multiplexer_5_out), .in1(multiplexer_7_out), .out(multiplexer_6_out), .sel(Function_3[1]));
  assign or_1_out = RS2 | RS1;  // OR_Gate or_1, 32 bits wide
  Multiplexer #(.width(32), .enable("false")) multiplexer_7 (
    .in0(or_1_out), .in1(and_1_out), .out(multiplexer_7_out), .sel(Function_3[0]));
  assign and_1_out = RS2 & RS1;  // AND_Gate and_1, 32 bits wide
endmodule

module ALU (
  input  [31:0] Rs1,
  input  [31:0] Rs2,
  input  Add_sub_sel,
  input  shift_select,
  input  [2:0] Fun3,
  input  BranchIns_1_0,
  input  IR___LS,
  output Overflow,
  output DO_Branch,
  output [31:0] ALU_OUT
);

  wire B_ALU_do_b;
  wire [2:0] demultiplexer_1_out0, demultiplexer_1_out1;
  wire [31:0] I_R_ALU_alu_out, LOAD_STORE_ALU_mem_address;

  Demultiplexer #(.width(3), .enable("false")) demultiplexer_1 (
    .out0(demultiplexer_1_out0), .out1(demultiplexer_1_out1), .in(Fun3), .sel(BranchIns_1_0));
  I_R_type_ALU I_R_ALU (
    .add_sub_sel(Add_sub_sel), .Shift_select(shift_select), .Overflow(Overflow),
    .Function_3(demultiplexer_1_out0), .RS2(Rs1), .RS1(Rs2), .ALU_OUT(I_R_ALU_alu_out));
  Multiplexer #(.width(32), .enable("false")) multiplexer_1 (
    .in0(I_R_ALU_alu_out), .in1(LOAD_STORE_ALU_mem_address), .out(ALU_OUT), .sel(IR___LS));
  B_type_ALU B_ALU (.Rs1(Rs1), .Rs2(Rs2), .Function_3(demultiplexer_1_out1), .DO_B(B_ALU_do_b));
  Store_ALU LOAD_STORE_ALU (.IMM(Rs1), .RS1(Rs2), .Mem_address(LOAD_STORE_ALU_mem_address));
  and and_1 (DO_Branch, B_ALU_do_b, BranchIns_1_0);

  // Notes on the sheet:
  //   ALU
endmodule

// Control Unit
module CU_2 (
  input  [6:0] Opcode,
  input  Do_branch,
  input  [2:0] Func_3,
  input  [6:0] Func7IN,
  output From_MEM,
  output LOAD_STORE_INS,
  output Reg_Write,
  output [1:0] Imm__src,
  output Mem_write,
  output Select_I_R,
  output BrnachINS,
  output lui_nor_imm,
  output LUIPC,
  output PC_src,
  output [2:0] Function_3,
  output ADD_sub,
  output Shifter
);

  wire and_1_out, and_3_out, and_4_out, and_7_out, and_8_out, and_10_out, not_1_out, not_2_out, not_3_out,
       not_4_out, not_5_out, not_6_out, not_7_out, not_8_out, not_9_out, not_10_out, not_11_out, not_12_out,
       not_13_out, not_14_out, not_15_out, not_16_out, not_17_out, not_18_out;

  not not_1 (not_1_out, Opcode[2]);
  and and_1 (and_1_out, Opcode[0], Opcode[1], Opcode[2], not_2_out, Opcode[4], Opcode[5], not_3_out);
  not not_2 (not_2_out, Opcode[3]);
  not not_3 (not_3_out, Opcode[6]);
  not not_4 (not_4_out, Opcode[3]);
  and and_2 (LUIPC, Opcode[0], Opcode[1], Opcode[2], not_4_out, Opcode[4], not_5_out, not_6_out);
  not not_5 (not_5_out, Opcode[5]);
  not not_6 (not_6_out, Opcode[6]);
  not not_7 (not_7_out, Opcode[4]);
  not not_8 (not_8_out, Opcode[4]);
  not not_9 (not_9_out, Opcode[5]);
  not not_10 (not_10_out, Opcode[6]);
  not not_11 (not_11_out, Opcode[6]);
  not not_12 (not_12_out, Opcode[5]);
  not not_13 (not_13_out, Opcode[6]);
  not not_14 (not_14_out, Opcode[4]);
  and and_3 (and_3_out, not_7_out, Opcode[5], Opcode[6]);
  and and_4 (and_4_out, not_11_out, Opcode[5], Opcode[4], not_1_out);
  not not_15 (not_15_out, Opcode[4]);
  and and_5 (BrnachINS, not_15_out, Opcode[5], Opcode[6]);
  not not_16 (not_16_out, Opcode[4]);
  not not_17 (not_17_out, Opcode[5]);
  and and_6 (From_MEM, not_16_out, not_17_out, not_18_out);
  not not_18 (not_18_out, Opcode[6]);
  and and_7 (and_7_out, not_12_out, not_13_out);
  or or_1 (Reg_Write, and_7_out, and_8_out);
  and and_8 (and_8_out, Opcode[4], not_13_out);
  and and_9 (Imm__src[1], not_14_out, not_13_out);
  or or_2 (Imm__src[0], Opcode[6], and_10_out);
  and and_10 (and_10_out, not_8_out, not_9_out);
  and and_11 (Mem_write, not_10_out, Opcode[5], not_8_out);
  or or_3 (Select_I_R, and_3_out, and_4_out);
  or or_4 (LOAD_STORE_INS, From_MEM, Mem_write);
  or or_5 (lui_nor_imm, and_1_out, LUIPC);

  assign ADD_sub = Func7IN[5];
  assign Function_3 = Func_3;
  assign PC_src = Do_branch;
  assign Shifter = Func7IN[5];

  // Notes on the sheet:
  //   1100011   Brnach
  //   0100011  STORE
  //   0000011  LOAD
  //   0010011  I type
  //   0110011 R type
  //   0110111  U type
  //   0010111  LUIPC type
  //   1101111  UJ type
  //   1101111  UJ type
  //   Contro Unit Inputs
  //   Contro Unit Outputs
  //   00   I TYPE
  //   01    B TYPE
  //   10    Store 
  //   11    LOAD
endmodule

module Store_ALU (
  input  [31:0] IMM,
  input  [31:0] RS1,
  output [31:0] Mem_address
);

  Adder #(.width(32)) adder_1 (.a(IMM), .b(RS1), .out(Mem_address));  // open: cin, cout
endmodule

module PC (
  input  PC_SRC,
  input  CLK,
  input  [31:0] Immidiate,
  output [11:0] Memory_address,
  output [31:0] TO_RD
);

  wire [31:0] adder_1_out, multiplexer_1_out;
  wire [31:12] counter_1_q;

  Adder #(.width(32)) adder_1 (
    .a(multiplexer_1_out), .b({counter_1_q, Memory_address}), .out(adder_1_out));  // open: cin, cout
  Multiplexer #(.width(32), .enable("false")) multiplexer_1 (
    .in0(32'h1), .in1(Immidiate), .out(multiplexer_1_out), .sel(PC_SRC));
  Counter #(.width(32), .max('hffffffff)) counter_1 (
    .load(1'b1), .D(adder_1_out), .count(1'b0), .Q({counter_1_q, Memory_address}), .clk(CLK));  // open: carry, clr
  Adder #(.width(32)) adder_2 (.a({counter_1_q, Memory_address}), .b(Immidiate), .out(TO_RD));  // open: cin, cout

  // Notes on the sheet:
  //   Program counter
endmodule

module Load_ins (
  input  [31:0] value_from_mem,
  input  [2:0] Fun3,
  output [31:0] Output
);

  wire [31:0] bit_extender_1_out, bit_extender_2_out, multiplexer_1_out, multiplexer_3_out, negator_1_out;

  assign bit_extender_1_out = {{24{value_from_mem[7]}}, value_from_mem[7:0]};  // Bit_Extender bit_extender_1
  assign bit_extender_2_out = {{16{value_from_mem[15]}}, value_from_mem[15:0]};  // Bit_Extender bit_extender_2
  Multiplexer #(.select(2), .width(32), .enable("false")) multiplexer_1 (
    .in0(bit_extender_1_out), .in1(bit_extender_2_out), .in2(value_from_mem), .out(multiplexer_1_out),
    .sel(Fun3[1:0]));  // open: in3
  Multiplexer #(.width(32), .enable("false")) multiplexer_2 (
    .in0(multiplexer_1_out), .in1(multiplexer_3_out), .out(Output), .sel(Fun3[2]));
  Negator #(.width(32)) negator_1 (.in(multiplexer_1_out), .out(negator_1_out));
  Multiplexer #(.width(32), .enable("false")) multiplexer_3 (
    .in0(multiplexer_1_out), .in1(negator_1_out), .out(multiplexer_3_out), .sel(multiplexer_1_out[31]));

  // Notes on the sheet:
  //   LOAD TYPE ALU
endmodule

module Store_Ins (
  input  [31:0] Reg_input,
  input  [2:0] Fun3,
  output [31:0] Data_Output
);

  wire [31:0] bit_extender_1_out, bit_extender_2_out;

  assign bit_extender_1_out = {{24{1'b0}}, Reg_input[7:0]};  // Bit_Extender bit_extender_1
  assign bit_extender_2_out = {{16{1'b0}}, Reg_input[15:0]};  // Bit_Extender bit_extender_2
  Multiplexer #(.select(2), .width(32), .enable("false")) multiplexer_1 (
    .in0(bit_extender_1_out), .in1(bit_extender_2_out), .in2(Reg_input), .out(Data_Output), .sel(Fun3[1:0]));  // open: in3

  // Notes on the sheet:
  //   STORE TYPE ALU
endmodule

module imm_generator_for_LUI (
  input  [19:0] _20_bit_in,
  output [31:0] _32_bit_out
);


  assign _32_bit_out = {_20_bit_in, {12{1'b0}}};

  // Notes on the sheet:
  //   Immediate generator for LUI 
endmodule
